// Logisim project 8x4RAM.circ as structural Verilog: 9 circuits, main circuit main
module main (
  input  [3:0] in_1,
  input  [2:0] in_2,
  input  in_3,
  output [3:0] out_4
);

  wire clock_1_out;

  Clock clock_1 (.out(clock_1_out));
  RAMEightTimesFour rameighttimesfour_1 (.Write(in_3), .Address(in_2), .in_4(clock_1_out), .Data(in_1), .out_5(out_4));

  // Notes on the sheet:
  //   Data
  //   Address
  //   Clock
  //   Write
endmodule

module threeToEightDecoder (
  input  Data,
  input  s1,
  input  s2,
  input  s3,
  output out_5,
  output out_6,
  output out_7,
  output out_8,
  output out_9,
  output out_10,
  output out_11,
  output out_12
);

  wire not_1_out, not_2_out, not_3_out;

  not not_1 (not_1_out, s1);
  not not_2 (not_2_out, s2);
  not not_3 (not_3_out, s3);
  and and_1 (out_5, not_1_out, not_2_out, not_3_out, Data);
  and and_2 (out_6, s1, not_2_out, not_3_out, Data);
  and and_3 (out_7, Data, s2, not_3_out, Data);
  and and_4 (out_8, s1, s2, not_3_out, Data);
  and and_5 (out_9, not_1_out, not_2_out, s3, Data);
  and and_6 (out_10, s1, not_2_out, s3, Data);
  and and_7 (out_11, not_1_out, s2, s3, Data);
  and and_8 (out_12, s1, s2, s3, Data);
endmodule

module eightToOneSelector (
  input  d0,
  input  d1,
  input  d2,
  input  d3,
  input  d4,
  input  d5,
  input  d6,
  input  d7,
  input  s0,
  input  s1,
  input  s2,
  output Output
);

  wire and_1_out, and_2_out, and_3_out, and_4_out, and_5_out, and_6_out, and_7_out, and_8_out, not_1_out,
       not_2_out, not_3_out;

  not not_1 (not_1_out, s0);
  not not_2 (not_2_out, s1);
  not not_3 (not_3_out, s2);
  and and_1 (and_1_out, d0, not_3_out, not_2_out, not_1_out);
  and and_2 (and_2_out, d1, s0, not_2_out, not_2_out);
  and and_3 (and_3_out, d2, not_1_out, s1, not_3_out);
  and and_4 (and_4_out, d3, s0, s1, not_3_out);
  and and_5 (and_5_out, d4, not_1_out, not_2_out, s2);
  and and_6 (and_6_out, d5, s0, not_2_out, s2);
  and and_7 (and_7_out, d6, not_1_out, s1, s2);
  and and_8 (and_8_out, d7, s0, s1, s2);
  or or_1 (Output, and_1_out, and_2_out, and_3_out, and_4_out, and_5_out, and_6_out, and_7_out, and_8_out);
endmodule

module dTypeFlipFlop (
  input  Value,
  input  Enable,
  output out_3
);

  wire and_1_out, and_2_out, not_1_out;

  not not_1 (not_1_out, Value);
  and and_1 (and_1_out, Enable, not_1_out);
  and and_2 (and_2_out, Value, Enable);
  SRNorLatch srnorlatch_1 (.reset(and_1_out), .Set(and_2_out), .Q(out_3));

  // Notes on the sheet:
  //   Output
endmodule

module SRNorLatch (
  input  reset,
  input  Set,
  output Q
);

  wire nor_2_out;

  nor nor_1 (Q, reset, nor_2_out);
  nor nor_2 (nor_2_out, Q, Set);

  // Notes on the sheet:
  //   not Q
endmodule

module EdgeTriggeredDFlipFLop (
  input  in_1,
  input  E,
  input  Clock,
  output Out
);

  wire and_1_out, dtypeflipflop_1_out_3, not_1_out;

  and and_1 (and_1_out, E, Clock);
  dTypeFlipFlop dtypeflipflop_1 (.Value(in_1), .Enable(and_1_out), .out_3(dtypeflipflop_1_out_3));
  not not_1 (not_1_out, Clock);
  dTypeFlipFlop dtypeflipflop_2 (.Value(dtypeflipflop_1_out_3), .Enable(not_1_out), .out_3(Out));

  // Notes on the sheet:
  //   D
endmodule

module FourBitRegister (
  input  [3:0] in_1,
  input  Enable,
  input  Clock,
  output [3:0] out_4
);

  EdgeTriggeredDFlipFLop edgetriggereddflipflop_1 (.in_1(in_1[0]), .E(Enable), .Clock(Clock), .Out(out_4[0]));
  EdgeTriggeredDFlipFLop edgetriggereddflipflop_2 (.in_1(in_1[1]), .E(Enable), .Clock(Clock), .Out(out_4[1]));
  EdgeTriggeredDFlipFLop edgetriggereddflipflop_3 (.in_1(in_1[2]), .E(Enable), .Clock(Clock), .Out(out_4[2]));
  EdgeTriggeredDFlipFLop edgetriggereddflipflop_4 (.in_1(in_1[3]), .E(Enable), .Clock(Clock), .Out(out_4[3]));

  // Notes on the sheet:
  //   Data
endmodule

module RAMEightTimesFour (
  input  [3:0] Data,
  input  [2:0] Address,
  input  Write,
  input  in_4,
  output [3:0] out_5
);

  wire threetoeightdecoder_1_out_5, threetoeightdecoder_1_out_6, threetoeightdecoder_1_out_7,
       threetoeightdecoder_1_out_8, threetoeightdecoder_1_out_9, threetoeightdecoder_1_out_10,
       threetoeightdecoder_1_out_11, threetoeightdecoder_1_out_12;
  wire [3:0] fourbitregister_1_out_4, fourbitregister_2_out_4, fourbitregister_3_out_4,
       fourbitregister_4_out_4, fourbitregister_5_out_4, fourbitregister_6_out_4, fourbitregister_7_out_4,
       fourbitregister_8_out_4;

  threeToEightDecoder threetoeightdecoder_1 (
    .Data(Write), .s1(Address[0]), .s2(Address[1]), .s3(Address[2]), .out_5(threetoeightdecoder_1_out_5),
    .out_6(threetoeightdecoder_1_out_6), .out_7(threetoeightdecoder_1_out_7),
    .out_8(threetoeightdecoder_1_out_8), .out_9(threetoeightdecoder_1_out_9),
    .out_10(threetoeightdecoder_1_out_10), .out_11(threetoeightdecoder_1_out_11),
    .out_12(threetoeightdecoder_1_out_12));
  FourBitRegister fourbitregister_1 (
    .Enable(threetoeightdecoder_1_out_5), .Clock(in_4), .in_1(Data), .out_4(fourbitregister_1_out_4));
  FourBitRegister fourbitregister_2 (
    .Enable(threetoeightdecoder_1_out_6), .Clock(in_4), .in_1(Data), .out_4(fourbitregister_2_out_4));
  FourBitRegister fourbitregister_3 (
    .Enable(threetoeightdecoder_1_out_7), .Clock(in_4), .in_1(Data), .out_4(fourbitregister_3_out_4));
  FourBitRegister fourbitregister_4 (
    .Enable(threetoeightdecoder_1_out_8), .Clock(in_4), .in_1(Data), .out_4(fourbitregister_4_out_4));
  FourBitRegister fourbitregister_5 (
    .Enable(threetoeightdecoder_1_out_9), .Clock(in_4), .in_1(Data), .out_4(fourbitregister_5_out_4));
  FourBitRegister fourbitregister_6 (
    .Enable(threetoeightdecoder_1_out_10), .Clock(in_4), .in_1(Data), .out_4(fourbitregister_6_out_4));
  FourBitRegister fourbitregister_7 (
    .Enable(threetoeightdecoder_1_out_11), .Clock(in_4), .in_1(Data), .out_4(fourbitregister_7_out_4));
  FourBitRegister fourbitregister_8 (
    .Enable(threetoeightdecoder_1_out_12), .Clock(in_4), .in_1(Data), .out_4(fourbitregister_8_out_4));
  FourBitEightOneSelector fourbiteightoneselector_1 (
    .in_1(Address), .d0(fourbitregister_1_out_4), .in_3(fourbitregister_2_out_4),
    .in_4(fourbitregister_3_out_4), .in_5(fourbitregister_4_out_4), .in_6(fourbitregister_5_out_4),
    .in_7(fourbitregister_6_out_4), .in_8(fourbitregister_7_out_4), .in_9(fourbitregister_8_out_4),
    .out_10(out_5));

  // Notes on the sheet:
  //   Clock
  //   R0
  //   R7
endmodule

module FourBitEightOneSelector (
  input  [2:0] in_1,
  input  [3:0] d0,
  input  [3:0] in_3,
  input  [3:0] in_4,
  input  [3:0] in_5,
  input  [3:0] in_6,
  input  [3:0] in_7,
  input  [3:0] in_8,
  input  [3:0] in_9,
  output [3:0] out_10
);

  eightToOneSelector eighttooneselector_1 (
    .d1(in_3[0]), .d2(in_4[0]), .d3(in_5[0]), .d4(in_6[0]), .d5(in_7[0]), .d0(d0[0]), .d6(in_8[0]),
    .d7(in_9[0]), .s0(in_1[0]), .s1(in_1[1]), .s2(in_1[2]), .Output(out_10[0]));
  eightToOneSelector eighttooneselector_2 (
    .d1(in_3[1]), .d2(in_4[1]), .d3(in_5[1]), .d4(in_6[1]), .d5(in_7[1]), .d0(d0[1]), .d6(in_8[1]),
    .d7(in_9[1]), .s0(in_1[0]), .s1(in_1[1]), .s2(in_1[2]), .Output(out_10[1]));
  eightToOneSelector eighttooneselector_3 (
    .d1(in_3[2]), .d2(in_4[2]), .d3(in_5[2]), .d4(in_6[2]), .d5(in_7[2]), .d0(d0[2]), .d6(in_8[2]),
    .d7(in_9[2]), .s0(in_1[0]), .s1(in_1[1]), .s2(in_1[2]), .Output(out_10[2]));
  eightToOneSelector eighttooneselector_4 (
    .d1(in_3[3]), .d2(in_4[3]), .d3(in_5[3]), .d4(in_6[3]), .d5(in_7[3]), .d0(d0[3]), .d6(in_8[3]),
    .d7(in_9[3]), .s0(in_1[0]), .s1(in_1[1]), .s2(in_1[2]), .Output(out_10[3]));

  // Notes on the sheet:
  //   Selector
  //   d7
  //   0th
  //   3rd bit
endmodule
